# Fritzing sketch cktdiagram (saved by Fritzing 0.9.3b)
circuit board: 8.46667cm x 5.64444cm
breadboards: 1

parts:
  Part1 = Arduino Uno (Rev3)
  Part2 = Rotoshield - Motor driver shield for Arduino
  R1 = Resistor [tolerance=±5% resistance=1k package=THT]
  R2 = Resistor [tolerance=±5% resistance=1k package=THT]
  R3 = Resistor [tolerance=±5% resistance=1k package=THT]
  Part3 = Bluetooth HC-05 Macho
  M1 = DC Motor
  M2 = DC Motor
  J1 = Basic Servo
  Part4 = Soil Moisture Sensor
  T1 = LM35 Temperature Sensor [thermistor_type=NTC package="TO92 [THT]"]

nets:
  N1: Part1.A0, T1.Vout
  N2: Part1.A1, Part2.A_IN_1, Part4.SIG
  N3: Part1.A2, Part2.A_IN_2
  N4: Part1.A3, Part2.A_IN_3
  N5: Part1.A4/SDA, Part2.A_IN_4
  N6: Part1.A5/SCL, Part2.A_IN_5
  N7: Part1.D8, Part2.DIG_8
  N8: Part1.D9_PWM, Part2.DIG_9, J1.pulse
  N9: Part1.D10_PWM/SS, Part2.DIG_10
  N10: Part1.D12/MISO, Part2.DIG_12
  N11: Part1.D13/SCK, Part2.DIG_13
  GND: Part1.GND, Part2.GND, R3.Pin_1, Part3.GND, J1.gnd, Part4.GND, T1.GND
  N12: Part1.AREF, Part2.AREF
  N13: Part1.D0/RX, Part2.DIG_0, Part3.TXD
  N14: Part1.D1/TX, Part2.DIG_1, R1.Pin_0
  N15: Part1.D2, Part2.DIG_2
  N16: Part1.D3_PWM, Part2.DIG_3
  N17: Part1.D4, Part2.DIG_4
  N18: Part1.D5_PWM, Part2.DIG_5
  N19: Part1.D6_PWM, Part2.DIG_6
  N20: Part1.D7, Part2.DIG_7
  N21: Part1.RESET, Part2.RESET
  3V3: Part1.3V3, Part2.+3V3
  VCC: Part1.5V, Part3.VCC, J1.vcc, T1.+Vs
  VIN: Part1.VIN, Part2.VIN
  N22: Part2.M1-2, M1.pin_1
  N23: Part2.M1-1, M1.pin_2
  N24: Part2.M2-2, M2.pin_1
  N25: Part2.M2-1, M2.pin_2
  +5V: Part2.+5V, Part4.VCC
  N26: R1.Pin_1, R2.Pin_0, Part3.RXD
  N27: R2.Pin_1, R3.Pin_0
